# Fritzing sketch leapmotion_v1 (saved by Fritzing 0.9.3b)

parts:
  Part1 = Arduino Uno (Rev3)
  hc-sr1 = hc-sr04
  hc-sr2 = hc-sr04

nets:
  N1: Part1.D2, hc-sr2.Trig
  N2: Part1.D3_PWM, hc-sr2.Echo
  N3: Part1.D4, hc-sr1.Trig
  N4: Part1.D5_PWM, hc-sr1.Echo
  VCC: Part1.5V, hc-sr1.VCC, hc-sr2.VCC
  GND: Part1.GND, hc-sr1.GND, hc-sr2.GND

notes:
  Orange: 5V
  Black: GND (Tierra)
  Blue: Trigger
  White: Echo
