# Fritzing sketch leapmotion_v2 (saved by Fritzing 0.9.3b)

parts:
  Part1 = Arduino Uno (Rev3)
  hc-sr1 = hc-sr04
  hc-sr2 = hc-sr04

nets:
  N1: Part1.D9_PWM, hc-sr2.Trig
  N2: Part1.D5_PWM, hc-sr1.Echo
  N3: Part1.D6_PWM, hc-sr2.Echo
  N4: Part1.D7, hc-sr1.Trig
  VCC: Part1.5V, hc-sr1.VCC, hc-sr2.VCC
  GND: Part1.GND, hc-sr1.GND, hc-sr2.GND

// code stored in the sketch: Py-Kinesis.ino
#include <NewPing.h>
int trig1=9;
int echo1=6;
int trig2=7;
int echo2=5;
int R;
int L;
NewPing right(9,6,50);
NewPing left(7,5,50);
void setup() {
  Serial.begin(9600);
  pinMode(9,OUTPUT);
  pinMode(8,OUTPUT);
  pinMode(6,INPUT);
  pinMode(5,INPUT);
 
}

void loop() {
  
  //Serial.println("hi,am arduino");
  R=right.ping_cm();
  L=left.ping_cm();
  //Serial.println(R);
  //Serial.println(L);
  
 if (R==0 && L==0){
 
    Serial.println('0');
  }
  
  else if(R<L){
    
    Serial.println('2');
  }
  else if(R>L){
    
    Serial.println('1');
    

  
  }
  
}
