# Fritzing sketch leapmotion_v3 (saved by Fritzing 0.9.3b)
breadboards: 1

parts:
  Part1 = Arduino Uno (Rev3)
  hc-sr1 = hc-sr04
  hc-sr2 = hc-sr04
  LCD1 = LCD screen
  R1 = Trimmer Potentiometer [maximum_resistance=10kΩ package=THT]
  R2 = Resistor [tolerance=±5% resistance=220 package=THT]

nets:
  N1: Part1.D8, LCD1.DB6
  N2: Part1.D9_PWM, LCD1.DB5
  N3: Part1.D10_PWM/SS, LCD1.DB4
  N4: Part1.D11_PWM/MOSI, LCD1.E
  N5: Part1.D12/MISO, LCD1.RS
  N6: Part1.D2, hc-sr2.Trig
  N7: Part1.D3_PWM, hc-sr2.Echo
  N8: Part1.D4, hc-sr1.Trig
  N9: Part1.D5_PWM, hc-sr1.Echo
  N10: Part1.D7, LCD1.DB7
  GND: Part1.GND, hc-sr1.GND, hc-sr2.GND, LCD1.VSS, LCD1.R/W, LCD1.LED-, R1.leg1
  VCC: hc-sr1.VCC, hc-sr2.VCC, R2.Pin_0
  N11: LCD1.VDD, R1.leg2
  N12: LCD1.V0, R1.wiper
  N13: LCD1.LED+, R2.Pin_1

notes:
  ####Sensores####
  Orange: 5V
  Black: GND (Tierra)
  Blue: Trigger
  White: Echo
